# Fritzing sketch BPM (saved by Fritzing 0.9.3b)
breadboards: 1

parts:
  J1 = Generic female header - 37 pins [form="♀ (female)" package=THT]
  R1 = Resistor [tolerance=±5% resistance=4.7k package="0805 [SMD]"]
  M2 = MAX30102
  R2 = Resistor [tolerance=±5% resistance=4.7k package="0805 [SMD]"]

nets:
  N1: J1.pin13, M2.SDA, R2.Pin_1
  N2: J1.pin14, R1.Pin_0, M2.VIN, R2.Pin_0
  N3: J1.pin25, M2.GND
  N4: J1.pin29, R1.Pin_1, M2.SCL

notes:
  4.7KOhm Resistors

custom parts:
  Generic female header - 37 pins: Generic female header
  MAX30102: Oximeter module using the MAX30102 chip. You may wish to read (and check your module) this post on power problems with these modules: https://reedpaper.wordpress.com/2018/08/22/pulse-oximeter-max30100-max30102-how-to-fix-wrong-board/ . As usual, if you want the mounting holes in pcb, you need to drag a hole over the pad in silkscreen to actually drill the hole (by default they are not drilled)
